# Fritzing sketch Dual Motor Control System (saved by Fritzing 1.0.4)
breadboards: 2

parts:
  A1 = L298N motor driver
  A2 = ESP32 38Pin narrow
  R1 = Rotary Potentiometer (Large) [maximum_resistance=10kΩ knob_status=50% power=0.5W package=THT]
  M1 = gear-motor
  M2 = gear-motor
  S1 = Pushbutton [package="[THT]"]
  S2 = Pushbutton [package="[THT]"]
  U1 = LIPO-110mAh [package=lipo-110]
  U2 = LIPO-110mAh [package=lipo-110]

nets:
  N1: A1.Motor_B_1, M2.pin_2
  N2: A1.Motor_B_2, M2.pin_1
  N3: A1.GND, U1.-, U2.-
  N4: A1.VMS, U1.+, U2.+
  N5: A1.Motor_A_1, M1.pin_2
  N6: A1.Motor_A_2, M1.pin_1
  N7: A1.ENA, A2.Pin_37
  N8: A1.IN1, A2.Pin_10
  N9: A1.IN2, A2.Pin_11
  N10: A1.IN3, A2.Pin_12
  N11: A1.IN4, A2.Pin_13
  N12: A1.ENB, A2.Pin_34
  N13: A2.Pin_1, R1.leg1
  N14: A2.Pin_5, R1.wiper
  N15: A2.Pin_14, A2.Pin_32, A2.Pin_38
  N16: A2.Pin_15, R1.leg2, S1.Pin_1, S1.Pin_2, S2.Pin_1, S2.Pin_2
  N17: A2.Pin_24, S2.Pin_3, S2.Pin_4
  N18: A2.Pin_25, S1.Pin_3, S1.Pin_4

custom parts:
  L298N motor driver: .The double-H driver module uses the ST L298N dual full-bridge driver, a monolithic integrated circuit in a 15-pin multiwatt, PowerSO20 package.
  ESP32 38Pin narrow: ESP32 38Pin narrow.

// code stored in the sketch: Fritzing Diagram Motor.ino
/* ============================================================
    Project: Dual Motor Control System (ESP32)
    Author:  Máximo Mancilla
    Date:    2025
    Description:
      Two buttons select motor direction (left / right),
      and a potentiometer controls speed via PWM.
      Both TT motors run through an H-bridge driver.
   ============================================================ */


/// --------------------- INPUT PINS --------------------------
int leftBut  = 0;
int rightBut = 4;
int pot      = 34;


/// ------------------- MOTOR DRIVER PINS ---------------------
int pwmMA = 22;   // Motor A PWM
int in1   = 25;
int in2   = 26;


int pwmMB = 21;   // Motor B PWM
int in3   = 27;
int in4   = 14;


/// ------------------ PWM CONFIGURATION ----------------------
int freq       = 5000;
int resolution = 8;
int channelA   = 0;
int channelB   = 1;


/// ---------------------- VARIABLES --------------------------
int leftVal;
int rightVal;
int potVal;


int motorSpeed;
int direction = 0;       // -1 = left, 1 = right, 0 = stopped
int minPWM    = 90;
int maxPWM    = 255;


/// ============================================================
///                         SETUP
/// ============================================================
void setup() {


  // Buttons with internal pullups
  pinMode(leftBut,  INPUT_PULLUP);
  pinMode(rightBut, INPUT_PULLUP);


  // Motor direction pins
  pinMode(in1, OUTPUT);
  pinMode(in2, OUTPUT);
  pinMode(in3, OUTPUT);
  pinMode(in4, OUTPUT);


  // Attach PWM to pins using the modern ESP32 function
  ledcAttach(pwmMA, freq, resolution);
  ledcAttach(pwmMB, freq, resolution);


  Serial.begin(115200);
  Serial.println("=== Dual Motor Control System Started ===");
}


/// ============================================================
///                          LOOP
/// ============================================================
void loop() {


  // Read inputs
  leftVal  = digitalRead(leftBut);
  rightVal = digitalRead(rightBut);
  potVal   = analogRead(pot);


  // Speed control with dead zone
  if (potVal < 200) {
    motorSpeed = 0;
  } else {
    motorSpeed = map(potVal, 200, 4095, minPWM, maxPWM);
  }


  // Direction control (buttons override)
  if (leftVal  == LOW) direction = -1;
  if (rightVal == LOW) direction = 1;


  // Apply direction to both motors
  if (direction == -1) {         // LEFT
    digitalWrite(in1, HIGH);
    digitalWrite(in2, LOW);
    digitalWrite(in3, HIGH);
    digitalWrite(in4, LOW);
  }
  else if (direction == 1) {     // RIGHT
    digitalWrite(in1, LOW);
    digitalWrite(in2, HIGH);
    digitalWrite(in3, LOW);
    digitalWrite(in4, HIGH);
  }
  else {                         // STOP
    digitalWrite(in1, LOW);
    digital
